// Logisim project 32_bit_register.circ as structural Verilog: 1 circuit, main circuit main
module main (
  input  [31:0] in_1,
  input  Input_EN,
  input  in_3
);

  wire clock_1_out;
  wire [31:0] register_1_q;

  Clock clock_1 (.out(clock_1_out));
  Register #(.width(32)) register_1 (.D(in_1), .en(Input_EN), .Q(register_1_q), .clk(clock_1_out), .clr(in_3));
  // Probe on register_1_q

  // Notes on the sheet:
  //   Input D
  //   Input CLR
  //   Clock
  //   Register
  //   Output Q
endmodule
